# Fritzing sketch Plant (saved by Fritzing 0.9.3b)
breadboards: 1

parts:
  Arduino_Mega = Arduino Mega 2560 (Rev3)
  LDR2 = Photocell (LDR) [package=THT]
  R2 = Resistor [tolerance=±5% resistance=10k package=THT]
  LDR3 = Photocell (LDR) [package=THT]
  R3 = Resistor [tolerance=±5% resistance=10k package=THT]
  LDR4 = Photocell (LDR) [package=THT]
  R4 = Resistor [tolerance=±5% resistance=10k package=THT]
  LDR1 = Photocell (LDR) [package=THT]
  R1 = Resistor [tolerance=±5% resistance=10k package=THT]
  IRF520 = MOSFET-NCHANNEL [package=to220v]
  12V_LED = smd LED [color="Red (633nm)" package="0603 [SMD]"]
  Power_Supply = DC Power [voltage=12V]
  IRF520_2 = MOSFET-NCHANNEL [package=to220v]
  12V_LED1 = smd LED [color="Red (633nm)" package="0603 [SMD]"]
  IRF520_3 = MOSFET-NCHANNEL [package=to220v]
  12V_LED2 = smd LED [color="Red (633nm)" package="0603 [SMD]"]
  IRF520_4 = MOSFET-NCHANNEL [package=to220v]
  12V_LED3 = smd LED [color="Red (633nm)" package="0603 [SMD]"]
  IRF520_5 = MOSFET-NCHANNEL [package=to220v]
  12V_LED4 = smd LED [color="Red (633nm)" package="0603 [SMD]"]
  IRF524 = MOSFET-NCHANNEL [package=to220v]
  12V_LED5 = smd LED [color="Red (633nm)" package="0603 [SMD]"]
  IRF525 = MOSFET-NCHANNEL [package=to220v]
  12V_LED6 = smd LED [color="Red (633nm)" package="0603 [SMD]"]
  IRF526 = MOSFET-NCHANNEL [package=to220v]
  12V_LED7 = smd LED [color="Red (633nm)" package="0603 [SMD]"]
  IRF527 = MOSFET-NCHANNEL [package=to220v]
  12V_LED8 = smd LED [color="Red (633nm)" package="0603 [SMD]"]
  PUMP_12V = DC Motor

nets:
  N1: Arduino_Mega.A8, LDR2.pin_1, R2.Pin_0
  N2: Arduino_Mega.A9, LDR1.pin_1, R1.Pin_0
  N3: Arduino_Mega.A6, LDR4.pin_1, R4.Pin_0
  N4: Arduino_Mega.A7, LDR3.pin_1, R3.Pin_0
  N5: Arduino_Mega.5V, R2.Pin_1, R3.Pin_1, R4.Pin_1, R1.Pin_1
  N6: Arduino_Mega.GND, LDR2.pin_0, LDR3.pin_0, LDR4.pin_0, LDR1.pin_0, IRF520.S, Power_Supply.V-, IRF520_2.S, IRF520_3.S, IRF520_4.S, IRF520_5.S, IRF524.S, IRF525.S, IRF526.S, IRF527.S, PUMP_12V.pin_2
  N7: Arduino_Mega.VIN, 12V_LED.anode, Power_Supply.V+, 12V_LED1.anode, 12V_LED2.anode, 12V_LED3.anode, 12V_LED4.anode, 12V_LED5.anode, 12V_LED6.anode, 12V_LED7.anode, 12V_LED8.anode, PUMP_12V.pin_1
  N8: Arduino_Mega.D22, IRF520.G
  N9: Arduino_Mega.D23, IRF520_2.G
  N10: Arduino_Mega.D24, IRF520_3.G
  N11: Arduino_Mega.D25, IRF520_4.G
  N12: Arduino_Mega.D26, IRF520_5.G
  N13: Arduino_Mega.D27, IRF524.G
  N14: Arduino_Mega.D28, IRF525.G
  N15: Arduino_Mega.D29, IRF526.G
  N16: Arduino_Mega.D30, IRF527.G
  N17: IRF520.D, 12V_LED.cathode
  N18: IRF520_2.D, 12V_LED1.cathode
  N19: IRF520_3.D, 12V_LED2.cathode
  N20: IRF520_4.D, 12V_LED3.cathode
  N21: IRF520_5.D, 12V_LED4.cathode
  N22: IRF524.D, 12V_LED5.cathode
  N23: IRF525.D, 12V_LED6.cathode
  N24: IRF526.D, 12V_LED7.cathode
  N25: IRF527.D, 12V_LED8.cathode

notes:
  NOT A Vin, but a PLUG CONNECTION
  LEAF 1
  LEAF 2
  LEAF 3
