# Fritzing sketch water_can_final 2 (saved by Fritzing 0.9.3b)
breadboards: 1

parts:
  Part1 = Arduino Nano (Rev3.0)
  BAT1 = BC9VPC [package=bc9vpc]
  S2 = Toggle Switch [package=THT]
  LED2 = LEDs [package=led10mm]
  LED3 = LEDs [package=led10mm]
  LED4 = LEDs [package=led10mm]
  Part2 = 9-DOF Absolute Orientation IMU Fusion Breakout - BNO055
  Q1 = MOSFET-NCHANNEL [package=to220v]
  IC1 = Voltage Regulator [package=78xxl]

nets:
  GND: Part1.GND, BAT1.V-, S2.COM, Part2.GND
  N1: Part1.D5, Q1.G
  N2: Part1.VIN, IC1.OUT
  N3: Part1.A5, Part2.SCL_5V
  N4: Part1.A4, Part2.SDA_5V
  N5: BAT1.V+, S2.L1, LED2.C, LED3.C, LED4.C, Part2.5.0V, Q1.S, IC1.GND, IC1.IN
  N6: LED2.A, LED3.A, LED4.A, Q1.D

custom parts:
  9-DOF Absolute Orientation IMU Fusion Breakout - BNO055: A MEMS accelerometer, magnetometer and gyroscope on a single die with a high speed ARM Cortex-M0 based processor to digest all the sensor data, abstract the sensor fusion and real time requirements away, and spit out data you can use in quaternions, Euler angles or vectors.
