# Fritzing sketch LCD&DHT22 (saved by Fritzing 0.9.3b)
breadboards: 1

parts:
  Part1 = Arduino Uno (Rev3)
  RHT1 = Humidity and Temperature Sensor RHT03
  R1 = Resistor [tolerance=±5% resistance=10k package=THT]
  LCD1 = LCD screen
  R2 = Resistor [tolerance=±5% resistance=220 package=THT]
  R3 = Rotary Potentiometer (Small) [maximum_resistance=10kΩ package=THT]

nets:
  N1: Part1.D11_PWM/MOSI, RHT1.Data-signal, R1.Pin_0
  GND: Part1.GND, RHT1.GND_2, LCD1.VSS, LCD1.LED-, R3.leg1
  N2: Part1.D2, LCD1.RS
  N3: Part1.D3_PWM, LCD1.E
  N4: Part1.D4, LCD1.DB4
  N5: Part1.D5_PWM, LCD1.DB5
  N6: Part1.D6_PWM, LCD1.DB6
  N7: Part1.D7, LCD1.DB7
  5V: Part1.5V, RHT1.Vcc, R1.Pin_1, LCD1.VDD, R2.Pin_1, R3.leg2
  N8: LCD1.V0, R3.wiper
